// Digital circuit 4 bit Program Counter.dig as structural Verilog
module _4_bit_Program_Counter (
  input  CLK,
  input  [3:0] I__3_0,
  output [3:0] O__3_0
);

  _1_bit_Reg _1_bit_reg_1 (.Din(I__3_0[0]), .Sel(1'b1), .CLK(CLK), .Dout(O__3_0[0]));
  _1_bit_Reg _1_bit_reg_2 (.Din(I__3_0[1]), .Sel(1'b1), .CLK(CLK), .Dout(O__3_0[1]));
  _1_bit_Reg _1_bit_reg_3 (.Din(I__3_0[2]), .Sel(1'b1), .CLK(CLK), .Dout(O__3_0[2]));
  _1_bit_Reg _1_bit_reg_4 (.Din(I__3_0[3]), .Sel(1'b1), .CLK(CLK), .Dout(O__3_0[3]));
endmodule
