// Digital circuit 6 bit CPU.dig as structural Verilog
module _6_bit_CPU (
  input  [3:0] WR__3_0,
  input  [16:0] WRD__16_0,
  input  WE,
  input  CLK,
  input  PC_EN,
  input  [3:0] RA2__3_0,
  input  SF,
  input  ZF,
  output [16:0] RD2__16_0,
  output [2:0] RB__2_0,
  output [2:0] RA__2_0,
  output [5:0] B__5_0,
  output [5:0] A__5_0,
  output [5:0] R__5_0,
  output [3:0] JMP_addr
);

  wire CPU_CLK, Imm_sel, JMP_sel, REG_EN;
  wire [1:0] Op;
  wire [3:0] _4_bit_pc_adder_1_o__3_0, _4_bit_program_counter_1_o__3_0, multiplexer_1_out;
  wire [5:0] _6_bit_reg_set_1_b_5_0;
  wire [6:0] XX;
  wire [16:13] _9x17_ram_1_rd1__16_0;

  Multiplexer #(.Bits(4)) multiplexer_1 (
    .sel(JMP_sel), .in_0(_4_bit_pc_adder_1_o__3_0), .in_1(JMP_addr), .out(multiplexer_1_out));
  _4_bit_PC_Adder _4_bit_pc_adder_1 (.I__3_0(_4_bit_program_counter_1_o__3_0), .O__3_0(_4_bit_pc_adder_1_o__3_0));
  _4_bit_Program_Counter _4_bit_program_counter_1 (
    .I__3_0(multiplexer_1_out), .CLK(CPU_CLK), .O__3_0(_4_bit_program_counter_1_o__3_0));
  and and_1 (CPU_CLK, PC_EN, CLK);
  _9x17_RAM _9x17_ram_1 (
    .RA1__3_0(_4_bit_program_counter_1_o__3_0), .RA2__3_0(RA2__3_0), .WR__3_0(WR__3_0),
    .WRD__16_0(WRD__16_0), .WE(WE), .CLK(CLK),
    .RD1__16_0({_9x17_ram_1_rd1__16_0, JMP_addr, RB__2_0[1:0], XX}), .RD2__16_0(RD2__16_0));
  _6_bit_CU _6_bit_cu_1 (
    .Opcode__3_0(_9x17_ram_1_rd1__16_0), .SF(SF), .ZF(ZF), .Op__1_0(Op), .REG_EN(REG_EN), .Imm_sel(Imm_sel),
    .JMP_sel(JMP_sel));
  _6_bit_reg_set _6_bit_reg_set_1 (
    .WRD__5_0(R__5_0), .CLK(CPU_CLK), .A_5_0(A__5_0), .B_5_0(_6_bit_reg_set_1_b_5_0),
    .RA__2_0(JMP_addr[3:1]), .RB__2_0({JMP_addr[0], RB__2_0[1:0]}), .WR__2_0(JMP_addr[3:1]), .WE(REG_EN));
  _6_bit_ALU _6_bit_alu_1 (.R_5_0(R__5_0), .OP_1_0(Op), .X_5_0(A__5_0), .Y_5_0(B__5_0));
  Multiplexer #(.Bits(6)) multiplexer_2 (
    .sel(Imm_sel), .in_0(_6_bit_reg_set_1_b_5_0), .in_1({JMP_addr[0], RB__2_0[1:0], XX[6:4]}), .out(B__5_0));

  assign RA__2_0 = JMP_addr[3:1];
  assign RB__2_0[2] = JMP_addr[0];

  // Other names for the same wires on the sheet: R2[2:0] = {JMP_addr[0], RB__2_0[1:0]}; R1[2:0] = JMP_addr[3:1];
  //   A[5:0] = A__5_0; B[5:0] = B__5_0; R[5:0] = R__5_0; RD2[16:0] = RD2__16_0

  // Notes on the sheet:
  //   Register Mode(Type of Op - 00) = 2bit (Type of Op) + 2bit (Op) + 3bit (Reg 1)+ 3bit (Reg 2) +  7bit (Don't care)
  //   Immidiate Mode(Type of Op - 01) = 2bit (Type of Op) + 2bit (Op) + 3bit (Reg 1)+ 6bit (Imm value) +4bit (Don't care)
  //   Jump Mode(Type of Op - 10) = 2bit (Type of Op) + 2bit (Op) + 4bit (Add) + 9 bit ( Don't care)
  //   ADD ( Op=00 ), OR ( Op=01 ), SHL ( Op=10 )
  //   JMP (Op = 00), JL ( Op=11)
  //   JMP Operation2 ->                         10 00 0010 000000000
  //   Operation 1: ADD R0,7 ->             01 00 000 000111 0000
  //   Operation 2: ADD R0,5 ->              01 00 000 000101 0000
  //   JL Operation2 ->                            10 11 0010 000000000
endmodule
