// Digital circuit 6 bit CU.dig as structural Verilog
module _6_bit_CU (
  input  [3:0] Opcode__3_0,
  input  SF,
  input  ZF,
  output [1:0] Op__1_0,
  output REG_EN,
  output Imm_sel,
  output JMP_sel
);

  wire and_1_out, and_3_out, and_4_out, and_5_out, or_2_out;

  and and_1 (and_1_out, ~Opcode__3_0[2], ~Opcode__3_0[3]);  // And
  and and_2 (Imm_sel, Opcode__3_0[2], ~Opcode__3_0[3]);  // And
  and and_3 (and_3_out, ~Opcode__3_0[2], Opcode__3_0[3]);  // And
  and and_4 (and_4_out, ~Opcode__3_0[0], ~Opcode__3_0[1]);  // And
  and and_5 (and_5_out, Opcode__3_0[0], Opcode__3_0[1], SF, ~ZF);  // And
  or or_1 (REG_EN, and_1_out, Imm_sel);
  or or_2 (or_2_out, and_4_out, and_5_out);
  and and_6 (JMP_sel, and_3_out, or_2_out);

  assign Op__1_0 = Opcode__3_0[1:0];
endmodule
