// Digital circuit 6 bit Full Adder.dig as structural Verilog
module _6_bit_Full_Adder (
  input  [5:0] X_5_0,
  input  [5:0] Y_5_0,
  output [5:0] R_5_0,
  output Cout
);

  wire C1, C2, C3, C4, C5;

  FA fa_1 (.X(X_5_0[5]), .Y(Y_5_0[5]), .S(R_5_0[5]), .Cin(C5), .Cout(Cout));
  FA fa_2 (.X(X_5_0[4]), .Y(Y_5_0[4]), .S(R_5_0[4]), .Cin(C4), .Cout(C5));
  FA fa_3 (.X(X_5_0[3]), .Y(Y_5_0[3]), .S(R_5_0[3]), .Cin(C3), .Cout(C4));
  FA fa_4 (.X(X_5_0[2]), .Y(Y_5_0[2]), .S(R_5_0[2]), .Cin(C2), .Cout(C3));
  FA fa_5 (.X(X_5_0[1]), .Y(Y_5_0[1]), .S(R_5_0[1]), .Cin(C1), .Cout(C2));
  FA fa_6 (.X(X_5_0[0]), .Y(Y_5_0[0]), .S(R_5_0[0]), .Cin(1'b0), .Cout(C1));
endmodule
