// Digital circuit 6 bit OR.dig as structural Verilog
module _6_bit_OR (
  input  [5:0] X_5_0,
  input  [5:0] Y_5_0,
  output [5:0] R_5_0
);

  or or_1 (R_5_0[5], X_5_0[0], Y_5_0[0]);
  or or_2 (R_5_0[4], X_5_0[1], Y_5_0[1]);
  or or_3 (R_5_0[3], X_5_0[2], Y_5_0[2]);
  or or_4 (R_5_0[2], X_5_0[3], Y_5_0[3]);
  or or_5 (R_5_0[1], X_5_0[4], Y_5_0[4]);
  or or_6 (R_5_0[0], X_5_0[5], Y_5_0[5]);

  // Other names for the same wires on the sheet: O0 = R_5_0[0]; O1 = R_5_0[1]; O2 = R_5_0[2]; O3 = R_5_0[3];
  //   O4 = R_5_0[4]; O5 = R_5_0[5]; X5 = X_5_0[0]; X4 = X_5_0[1]; X3 = X_5_0[2]; X2 = X_5_0[3]; X1 = X_5_0[4];
  //   X0 = X_5_0[5]; Y5 = Y_5_0[0]; Y4 = Y_5_0[1]; Y3 = Y_5_0[2]; Y2 = Y_5_0[3]; Y1 = Y_5_0[4]; Y0 = Y_5_0[5]
endmodule
