// Digital circuit 6 bit reg set.dig as structural Verilog
module _6_bit_reg_set (
  input  CLK,
  input  [2:0] RA__2_0,
  input  [2:0] RB__2_0,
  input  [5:0] WRD__5_0,
  input  [2:0] WR__2_0,
  input  WE,
  output [5:0] A_5_0,
  output [5:0] B_5_0
);

  wire D0, D1, D2, D3, D4, W0, W1, W2, W3, W4;
  wire [5:0] R0, R1, R2, R3, R4;

  Decoder #(.Selector_Bits(3)) decoder_1 (
    .sel(WR__2_0), .out_0(W0), .out_1(W1), .out_2(W2), .out_3(W3), .out_4(W4));  // open: out_5, out_6, out_7
  and and_1 (D4, W4, WE);
  and and_2 (D3, W3, WE);
  and and_3 (D2, W2, WE);
  and and_4 (D1, W1, WE);
  and and_5 (D0, W0, WE);
  _6_bit_Reg _6_bit_reg_1 (.Din_5_0(WRD__5_0), .Sel(D4), .CLK(CLK), .Dout_5_0(R4));
  _6_bit_Reg _6_bit_reg_2 (.Din_5_0(WRD__5_0), .Sel(D3), .CLK(CLK), .Dout_5_0(R3));
  _6_bit_Reg _6_bit_reg_3 (.Din_5_0(WRD__5_0), .Sel(D2), .CLK(CLK), .Dout_5_0(R2));
  _6_bit_Reg _6_bit_reg_4 (.Din_5_0(WRD__5_0), .Sel(D1), .CLK(CLK), .Dout_5_0(R1));
  _6_bit_Reg _6_bit_reg_5 (.Din_5_0(WRD__5_0), .Sel(D0), .CLK(CLK), .Dout_5_0(R0));
  Multiplexer #(.Selector_Bits(3), .Bits(6)) multiplexer_1 (
    .sel(RA__2_0), .in_0(R0), .in_1(R1), .in_2(R2), .in_3(R3), .in_4(R4), .in_5({6{1'b0}}), .in_6({6{1'b0}}),
    .in_7({6{1'b0}}), .out(A_5_0));
  Multiplexer #(.Selector_Bits(3), .Bits(6)) multiplexer_2 (
    .sel(RB__2_0), .in_0(R0), .in_1(R1), .in_2(R2), .in_3(R3), .in_4(R4), .in_5({6{1'b0}}), .in_6({6{1'b0}}),
    .in_7({6{1'b0}}), .out(B_5_0));
endmodule
