// Digital circuit 6 bit shl.dig as structural Verilog
module _6_bit_shl (
  input  [5:0] X_5_0,
  input  [5:0] Y_5_0,
  output [5:0] R_5_0
);

  Multiplexer #(.Selector_Bits(6)) multiplexer_1 (
    .sel(Y_5_0), .in_0(X_5_0[5]), .in_1(X_5_0[4]), .in_2(X_5_0[3]), .in_3(X_5_0[2]), .in_4(X_5_0[1]),
    .in_5(X_5_0[0]), .in_6(1'b0), .in_7(1'b0), .in_8(1'b0), .in_9(1'b0), .in_10(1'b0), .in_11(1'b0),
    .in_12(1'b0), .in_13(1'b0), .in_14(1'b0), .in_15(1'b0), .in_16(1'b0), .in_17(1'b0), .in_18(1'b0),
    .in_19(1'b0), .in_20(1'b0), .in_21(1'b0), .in_22(1'b0), .in_23(1'b0), .in_24(1'b0), .in_25(1'b0),
    .in_26(1'b0), .in_27(1'b0), .in_28(1'b0), .in_29(1'b0), .in_30(1'b0), .in_31(1'b0), .in_32(1'b0),
    .in_33(1'b0), .in_34(1'b0), .in_35(1'b0), .in_36(1'b0), .in_37(1'b0), .in_38(1'b0), .in_39(1'b0),
    .in_40(1'b0), .in_41(1'b0), .in_42(1'b0), .in_43(1'b0), .in_44(1'b0), .in_45(1'b0), .in_46(1'b0),
    .in_47(1'b0), .in_48(1'b0), .in_49(1'b0), .in_50(1'b0), .in_51(1'b0), .in_52(1'b0), .in_53(1'b0),
    .in_54(1'b0), .in_55(1'b0), .in_56(1'b0), .in_57(1'b0), .in_58(1'b0), .in_59(1'b0), .in_60(1'b0),
    .in_61(1'b0), .in_62(1'b0), .in_63(1'b0), .out(R_5_0[5]));
  Multiplexer #(.Selector_Bits(6)) multiplexer_2 (
    .sel(Y_5_0), .in_0(X_5_0[3]), .in_1(X_5_0[2]), .in_2(X_5_0[1]), .in_3(X_5_0[0]), .in_4(1'b0),
    .in_5(1'b0), .in_6(1'b0), .in_7(1'b0), .in_8(1'b0), .in_9(1'b0), .in_10(1'b0), .in_11(1'b0),
    .in_12(1'b0), .in_13(1'b0), .in_14(1'b0), .in_15(1'b0), .in_16(1'b0), .in_17(1'b0), .in_18(1'b0),
    .in_19(1'b0), .in_20(1'b0), .in_21(1'b0), .in_22(1'b0), .in_23(1'b0), .in_24(1'b0), .in_25(1'b0),
    .in_26(1'b0), .in_27(1'b0), .in_28(1'b0), .in_29(1'b0), .in_30(1'b0), .in_31(1'b0), .in_32(1'b0),
    .in_33(1'b0), .in_34(1'b0), .in_35(1'b0), .in_36(1'b0), .in_37(1'b0), .in_38(1'b0), .in_39(1'b0),
    .in_40(1'b0), .in_41(1'b0), .in_42(1'b0), .in_43(1'b0), .in_44(1'b0), .in_45(1'b0), .in_46(1'b0),
    .in_47(1'b0), .in_48(1'b0), .in_49(1'b0), .in_50(1'b0), .in_51(1'b0), .in_52(1'b0), .in_53(1'b0),
    .in_54(1'b0), .in_55(1'b0), .in_56(1'b0), .in_57(1'b0), .in_58(1'b0), .in_59(1'b0), .in_60(1'b0),
    .in_61(1'b0), .in_62(1'b0), .in_63(1'b0), .out(R_5_0[3]));
  Multiplexer #(.Selector_Bits(6)) multiplexer_3 (
    .sel(Y_5_0), .in_0(X_5_0[1]), .in_1(X_5_0[0]), .in_2(1'b0), .in_3(1'b0), .in_4(1'b0), .in_5(1'b0),
    .in_6(1'b0), .in_7(1'b0), .in_8(1'b0), .in_9(1'b0), .in_10(1'b0), .in_11(1'b0), .in_12(1'b0),
    .in_13(1'b0), .in_14(1'b0), .in_15(1'b0), .in_16(1'b0), .in_17(1'b0), .in_18(1'b0), .in_19(1'b0),
    .in_20(1'b0), .in_21(1'b0), .in_22(1'b0), .in_23(1'b0), .in_24(1'b0), .in_25(1'b0), .in_26(1'b0),
    .in_27(1'b0), .in_28(1'b0), .in_29(1'b0), .in_30(1'b0), .in_31(1'b0), .in_32(1'b0), .in_33(1'b0),
    .in_34(1'b0), .in_35(1'b0), .in_36(1'b0), .in_37(1'b0), .in_38(1'b0), .in_39(1'b0), .in_40(1'b0),
    .in_41(1'b0), .in_42(1'b0), .in_43(1'b0), .in_44(1'b0), .in_45(1'b0), .in_46(1'b0), .in_47(1'b0),
    .in_48(1'b0), .in_49(1'b0), .in_50(1'b0), .in_51(1'b0), .in_52(1'b0), .in_53(1'b0), .in_54(1'b0),
    .in_55(1'b0), .in_56(1'b0), .in_57(1'b0), .in_58(1'b0), .in_59(1'b0), .in_60(1'b0), .in_61(1'b0),
    .in_62(1'b0), .in_63(1'b0), .out(R_5_0[1]));
  Multiplexer #(.Selector_Bits(6)) multiplexer_4 (
    .sel(Y_5_0), .in_0(X_5_0[2]), .in_1(X_5_0[1]), .in_2(X_5_0[0]), .in_3(1'b0), .in_4(1'b0), .in_5(1'b0),
    .in_6(1'b0), .in_7(1'b0), .in_8(1'b0), .in_9(1'b0), .in_10(1'b0), .in_11(1'b0), .in_12(1'b0),
    .in_13(1'b0), .in_14(1'b0), .in_15(1'b0), .in_16(1'b0), .in_17(1'b0), .in_18(1'b0), .in_19(1'b0),
    .in_20(1'b0), .in_21(1'b0), .in_22(1'b0), .in_23(1'b0), .in_24(1'b0), .in_25(1'b0), .in_26(1'b0),
    .in_27(1'b0), .in_28(1'b0), .in_29(1'b0), .in_30(1'b0), .in_31(1'b0), .in_32(1'b0), .in_33(1'b0),
    .in_34(1'b0), .in_35(1'b0), .in_36(1'b0), .in_37(1'b0), .in_38(1'b0), .in_39(1'b0), .in_40(1'b0),
    .in_41(1'b0), .in_42(1'b0), .in_43(1'b0), .in_44(1'b0), .in_45(1'b0), .in_46(1'b0), .in_47(1'b0),
    .in_48(1'b0), .in_49(1'b0), .in_50(1'b0), .in_51(1'b0), .in_52(1'b0), .in_53(1'b0), .in_54(1'b0),
    .in_55(1'b0), .in_56(1'b0), .in_57(1'b0), .in_58(1'b0), .in_59(1'b0), .in_60(1'b0), .in_61(1'b0),
    .in_62(1'b0), .in_63(1'b0), .out(R_5_0[2]));
  Multiplexer #(.Selector_Bits(6)) multiplexer_5 (
    .sel(Y_5_0), .in_0(X_5_0[0]), .in_1(1'b0), .in_2(1'b0), .in_3(1'b0), .in_4(1'b0), .in_5(1'b0),
    .in_6(1'b0), .in_7(1'b0), .in_8(1'b0), .in_9(1'b0), .in_10(1'b0), .in_11(1'b0), .in_12(1'b0),
    .in_13(1'b0), .in_14(1'b0), .in_15(1'b0), .in_16(1'b0), .in_17(1'b0), .in_18(1'b0), .in_19(1'b0),
    .in_20(1'b0), .in_21(1'b0), .in_22(1'b0), .in_23(1'b0), .in_24(1'b0), .in_25(1'b0), .in_26(1'b0),
    .in_27(1'b0), .in_28(1'b0), .in_29(1'b0), .in_30(1'b0), .in_31(1'b0), .in_32(1'b0), .in_33(1'b0),
    .in_34(1'b0), .in_35(1'b0), .in_36(1'b0), .in_37(1'b0), .in_38(1'b0), .in_39(1'b0), .in_40(1'b0),
    .in_41(1'b0), .in_42(1'b0), .in_43(1'b0), .in_44(1'b0), .in_45(1'b0), .in_46(1'b0), .in_47(1'b0),
    .in_48(1'b0), .in_49(1'b0), .in_50(1'b0), .in_51(1'b0), .in_52(1'b0), .in_53(1'b0), .in_54(1'b0),
    .in_55(1'b0), .in_56(1'b0), .in_57(1'b0), .in_58(1'b0), .in_59(1'b0), .in_60(1'b0), .in_61(1'b0),
    .in_62(1'b0), .in_63(1'b0), .out(R_5_0[0]));
  Multiplexer #(.Selector_Bits(6)) multiplexer_6 (
    .sel(Y_5_0), .in_0(X_5_0[4]), .in_1(X_5_0[3]), .in_2(X_5_0[2]), .in_3(X_5_0[1]), .in_4(X_5_0[0]),
    .in_5(1'b0), .in_6(1'b0), .in_7(1'b0), .in_8(1'b0), .in_9(1'b0), .in_10(1'b0), .in_11(1'b0),
    .in_12(1'b0), .in_13(1'b0), .in_14(1'b0), .in_15(1'b0), .in_16(1'b0), .in_17(1'b0), .in_18(1'b0),
    .in_19(1'b0), .in_20(1'b0), .in_21(1'b0), .in_22(1'b0), .in_23(1'b0), .in_24(1'b0), .in_25(1'b0),
    .in_26(1'b0), .in_27(1'b0), .in_28(1'b0), .in_29(1'b0), .in_30(1'b0), .in_31(1'b0), .in_32(1'b0),
    .in_33(1'b0), .in_34(1'b0), .in_35(1'b0), .in_36(1'b0), .in_37(1'b0), .in_38(1'b0), .in_39(1'b0),
    .in_40(1'b0), .in_41(1'b0), .in_42(1'b0), .in_43(1'b0), .in_44(1'b0), .in_45(1'b0), .in_46(1'b0),
    .in_47(1'b0), .in_48(1'b0), .in_49(1'b0), .in_50(1'b0), .in_51(1'b0), .in_52(1'b0), .in_53(1'b0),
    .in_54(1'b0), .in_55(1'b0), .in_56(1'b0), .in_57(1'b0), .in_58(1'b0), .in_59(1'b0), .in_60(1'b0),
    .in_61(1'b0), .in_62(1'b0), .in_63(1'b0), .out(R_5_0[4]));

  // Other names for the same wires on the sheet: O0 = R_5_0[0]; O1 = R_5_0[1]; O2 = R_5_0[2]; O3 = R_5_0[3];
  //   O4 = R_5_0[4]; O5 = R_5_0[5]; Sel[5:0] = Y_5_0; X0 = X_5_0[0]; X1 = X_5_0[1]; X2 = X_5_0[2]; X3 = X_5_0[3];
  //   X4 = X_5_0[4]; X5 = X_5_0[5]
endmodule
