// Digital circuit 9x17 RAM.dig as structural Verilog
module _9x17_RAM (
  input  [3:0] RA1__3_0,
  input  [3:0] RA2__3_0,
  input  [3:0] WR__3_0,
  input  [16:0] WRD__16_0,
  input  WE,
  input  CLK,
  output [16:0] RD1__16_0,
  output [16:0] RD2__16_0
);

  wire D0, D1, D2, D3, D4, D5, D6, D7, D8, R1_0, R1_1, R1_2, R1_3, R1_4, R1_5, R1_6, R1_7, R1_8, R2_0, R2_1,
       R2_2, R2_3, R2_4, R2_5, R2_6, R2_7, R2_8, W0, W1, W2, W3, W4, W5, W6, W7, W8;
  wire [16:0] RD1_0, RD1_1, RD1_2, RD1_3, RD1_4, RD1_5, RD1_6, RD1_7, RD1_8, RD2_0, RD2_1, RD2_2, RD2_3,
       RD2_4, RD2_5, RD2_6, RD2_7, RD2_8;

  Decoder #(.Selector_Bits(4)) decoder_1 (
    .sel(RA1__3_0), .out_0(R1_0), .out_1(R1_1), .out_2(R1_2), .out_3(R1_3), .out_4(R1_4), .out_5(R1_5),
    .out_6(R1_6), .out_7(R1_7), .out_8(R1_8));  // open: out_9, out_10, out_11, out_12, out_13, out_14, out_15
  Decoder #(.Selector_Bits(4)) decoder_2 (
    .sel(WR__3_0), .out_0(W0), .out_1(W1), .out_2(W2), .out_3(W3), .out_4(W4), .out_5(W5), .out_6(W6),
    .out_7(W7), .out_8(W8));  // open: out_9, out_10, out_11, out_12, out_13, out_14, out_15
  and and_1 (D4, W4, WE);
  and and_2 (D3, W3, WE);
  and and_3 (D2, W2, WE);
  and and_4 (D1, W1, WE);
  and and_5 (D0, W0, WE);
  Decoder #(.Selector_Bits(4)) decoder_3 (
    .sel(RA2__3_0), .out_0(R2_0), .out_1(R2_1), .out_2(R2_2), .out_3(R2_3), .out_4(R2_4), .out_5(R2_5),
    .out_6(R2_6), .out_7(R2_7), .out_8(R2_8));  // open: out_9, out_10, out_11, out_12, out_13, out_14, out_15
  and and_6 (D8, W8, WE);
  and and_7 (D7, W7, WE);
  and and_8 (D6, W6, WE);
  and and_9 (D5, W5, WE);
  _1x17_RAM _1x17_ram_1 (
    .RS1(R1_8), .RS2(R2_8), .WS(D8), .WD_16_0(WRD__16_0), .CLK(CLK), .RD1__16_0(RD1_8), .RD2__16_0(RD2_8));
  _1x17_RAM _1x17_ram_2 (
    .RS1(R1_7), .RS2(R2_7), .WS(D7), .WD_16_0(WRD__16_0), .CLK(CLK), .RD1__16_0(RD1_7), .RD2__16_0(RD2_7));
  _1x17_RAM _1x17_ram_3 (
    .RS1(R1_6), .RS2(R2_6), .WS(D6), .WD_16_0(WRD__16_0), .CLK(CLK), .RD1__16_0(RD1_6), .RD2__16_0(RD2_6));
  _1x17_RAM _1x17_ram_4 (
    .RS1(R1_5), .RS2(R2_5), .WS(D5), .WD_16_0(WRD__16_0), .CLK(CLK), .RD1__16_0(RD1_5), .RD2__16_0(RD2_5));
  _1x17_RAM _1x17_ram_5 (
    .RS1(R1_4), .RS2(R2_4), .WS(D4), .WD_16_0(WRD__16_0), .CLK(CLK), .RD1__16_0(RD1_4), .RD2__16_0(RD2_4));
  _1x17_RAM _1x17_ram_6 (
    .RS1(R1_3), .RS2(R2_3), .WS(D3), .WD_16_0(WRD__16_0), .CLK(CLK), .RD1__16_0(RD1_3), .RD2__16_0(RD2_3));
  _1x17_RAM _1x17_ram_7 (
    .RS1(R1_2), .RS2(R2_2), .WS(D2), .WD_16_0(WRD__16_0), .CLK(CLK), .RD1__16_0(RD1_2), .RD2__16_0(RD2_2));
  _1x17_RAM _1x17_ram_8 (
    .RS1(R1_1), .RS2(R2_1), .WS(D1), .WD_16_0(WRD__16_0), .CLK(CLK), .RD1__16_0(RD1_1), .RD2__16_0(RD2_1));
  _1x17_RAM _1x17_ram_9 (
    .RS1(R1_0), .RS2(R2_0), .WS(D0), .WD_16_0(WRD__16_0), .CLK(CLK), .RD1__16_0(RD1_0), .RD2__16_0(RD2_0));
  assign RD1__16_0 = RD1_8 | RD1_7 | RD1_6 | RD1_5 | RD1_4 | RD1_3 | RD1_2 | RD1_1 | RD1_0;  // Or or_1, 17 bits wide
  assign RD2__16_0 = RD2_8 | RD2_7 | RD2_6 | RD2_5 | RD2_4 | RD2_3 | RD2_2 | RD2_1 | RD2_0;  // Or or_2, 17 bits wide

  // Other names for the same wires on the sheet: WR[3:0] = WR__3_0; WRD[16:0] = WRD__16_0
endmodule
